// Logisim project Tugas 8 Bit CPU Mic-1.circ as structural Verilog: 4 circuits, main circuit ALU
module ALU (
  input  [7:0] A,
  input  [7:0] B,
  input  [2:0] Op,
  output [7:0] C
);

  wire [7:0] adder_1_out, adder_2_out, adder_3_out, and_1_out, or_1_out, subtractor_1_out;

  Adder adder_1 (.a(A), .b(8'h1), .out(adder_1_out));  // open: cin, cout
  Adder adder_2 (.a(B), .b(8'h1), .out(adder_2_out));  // open: cin, cout
  Adder adder_3 (.a(A), .b(B), .out(adder_3_out));  // open: cin, cout
  Subtractor subtractor_1 (.a(A), .b(B), .out(subtractor_1_out));  // open: bin, bout
  assign and_1_out = A & B;  // AND_Gate and_1, 8 bits wide
  assign or_1_out = A | B;  // OR_Gate or_1, 8 bits wide
  Multiplexer #(.select(3), .width(8)) multiplexer_1 (
    .in0(A), .in1(B), .in2(adder_1_out), .in3(adder_2_out), .in4(adder_3_out), .in5(subtractor_1_out),
    .in6(and_1_out), .in7(or_1_out), .out(C), .sel(Op));  // open: en
endmodule

module Datapath (
  input  in_1,
  input  [7:0] in_2,
  input  in_3,
  input  in_4,
  input  [7:0] in_5,
  input  in_6,
  input  [1:0] in_7,
  input  in_8,
  input  [2:0] in_9,
  output [7:0] out_10
);

  wire clock_1_out;
  wire [7:0] A_q, ALU_c, B_q, MBR_q, multiplexer_1_out, PC_q;

  Clock clock_1 (.out(clock_1_out));
  Register PC (.D(ALU_c), .en(in_1), .Q(PC_q), .clk(clock_1_out));  // open: clr
  Register MBR (.D(in_2), .en(in_3), .Q(MBR_q), .clk(clock_1_out));  // open: clr
  Register OUT (.D(ALU_c), .en(in_4), .Q(out_10), .clk(clock_1_out));  // open: clr
  Register B (.D(ALU_c), .en(in_6), .Q(B_q), .clk(clock_1_out));  // open: clr
  Register A (.D(ALU_c), .en(in_8), .Q(A_q), .clk(clock_1_out));  // open: clr
  Multiplexer #(.select(2), .width(8)) multiplexer_1 (
    .in0(B_q), .in1(MBR_q), .in2(PC_q), .in3(in_5), .out(multiplexer_1_out), .sel(in_7));  // open: en
  ALU ALU (.A(A_q), .B(multiplexer_1_out), .Op(in_9), .C(ALU_c));
endmodule

module Control_Unit (
  input  [7:0] Ext_data_bus,
  input  in_2,
  input  [7:0] Ext_switch_input,
  output [7:0] Ext_add_bus,
  output [7:0] Out
);

  wire JMPC, MBR_en, OUT_en, PC_en, RA_en, RB_en;
  wire [1:0] ALU_sel;
  wire [2:0] OP_code;
  wire [4:0] bitselector_1_out, MIR, MPC_q, multiplexer_2_out;
  wire [7:0] A_q, ALU_c, B_q, MBR_q, multiplexer_1_out;
  wire [15:0] rom_1_data;

  Register PC (.D(ALU_c), .en(PC_en), .Q(Ext_add_bus), .clk(in_2));  // open: clr
  Register u_OUT (.D(ALU_c), .en(OUT_en), .Q(Out), .clk(in_2));  // open: clr
  Register B (.D(ALU_c), .en(RB_en), .Q(B_q), .clk(in_2));  // open: clr
  Register A (.D(ALU_c), .en(RA_en), .Q(A_q), .clk(in_2));  // open: clr
  Register MBR (.D(Ext_data_bus), .en(MBR_en), .Q(MBR_q), .clk(in_2));  // open: clr
  BitSelector #(.group(5)) bitselector_1 (.in(MBR_q), .out(bitselector_1_out), .sel(1'b0));
  Multiplexer #(.select(2), .width(8)) multiplexer_1 (
    .in0(B_q), .in1(MBR_q), .in2(Ext_add_bus), .in3(Ext_switch_input), .out(multiplexer_1_out), .sel(ALU_sel));  // open: en
  ALU ALU (.A(A_q), .B(multiplexer_1_out), .Op(OP_code), .C(ALU_c));
  Multiplexer #(.width(5)) multiplexer_2 (
    .in0(MIR), .in1(bitselector_1_out), .out(multiplexer_2_out), .sel(JMPC));  // open: en
  Register #(.width(5)) MPC (.D(multiplexer_2_out), .Q(MPC_q), .clk(in_2));  // open: en, clr
  ROM #(.addrWidth(5), .dataWidth(16)) rom_1 (.addr(MPC_q), .data(rom_1_data));  // open: sel
  Register #(.width(16), .trigger("falling")) u_MIR (
    .D(rom_1_data), .Q({MIR, JMPC, OP_code, RA_en, RB_en, OUT_en, PC_en, MBR_en, ALU_sel}), .clk(in_2));  // open: en, clr

  // Notes on the sheet:
  //   contents of rom_1 (hex, n*v repeats v):
  //   886 118a 400 0 c3 10 3804 89 4804 50c1 18a 140 60 240 7000
endmodule

module CPU_Mic_1 (
  input  [7:0] in_1
);

  wire clock_1_out;
  wire [7:0] Control_Unit_ext_add_bus, Control_Unit_out, rom_1_data;

  Clock clock_1 (.out(clock_1_out));
  ROM rom_1 (.addr(Control_Unit_ext_add_bus), .data(rom_1_data));  // open: sel
  Control_Unit Control_Unit (
    .Ext_data_bus(rom_1_data), .in_2(clock_1_out), .Ext_add_bus(Control_Unit_ext_add_bus),
    .Out(Control_Unit_out), .Ext_switch_input(in_1));
  Hex_Digit_Display hex_digit_display_1 (.value(Control_Unit_out[3:0]));  // open: dp
  Hex_Digit_Display hex_digit_display_2 (.value(Control_Unit_out[7:4]));  // open: dp

  // Notes on the sheet:
  //   contents of rom_1 (hex, n*v repeats v):
  //   8 1 5 b 6 2
endmodule
