// Logisim project Tugas 8 Bit CPU SAP 1.circ as structural Verilog: 3 circuits, main circuit ALU
module ALU (
  input  [7:0] in_1,
  input  [7:0] in_2,
  input  [3:0] in_3,
  output [7:0] out_4
);

  wire [7:0] adder_1_out, adder_2_out, adder_3_out, not_1_out;

  assign not_1_out = ~in_2;  // NOT_Gate not_1, 8 bits wide
  Adder adder_1 (.a(not_1_out), .b(8'h1), .out(adder_1_out));  // open: cin, cout
  Adder adder_2 (.a(in_1), .b(adder_1_out), .out(adder_2_out));  // open: cin, cout
  Adder adder_3 (.a(in_1), .b(in_2), .out(adder_3_out));  // open: cin, cout
  Multiplexer #(.select(4), .width(8)) multiplexer_1 (
    .in0(adder_3_out), .in1(adder_2_out), .out(out_4), .sel(in_3));  // open: in2, in3, in4, in5, in6, in7, in8, in9, in10, in11, in12, in13, in14, in15, en
endmodule

module CU (
  input  in_1,
  input  [3:0] in_2,
  output [7:0] out_3,
  output [15:0] out_4
);

  wire and_1_out, and_2_out, and_3_out, and_4_out, and_5_out, not_1_out, not_2_out, not_3_out, not_4_out,
       not_5_out, not_6_out, not_7_out, not_8_out, not_9_out, not_10_out, not_11_out, or_1_out;
  wire [7:0] counter_2_q, multiplexer_1_out, rom_1_data;

  not not_1 (not_1_out, and_1_out);
  Counter counter_1 (.load(and_1_out), .D({8{1'b0}}), .count(not_1_out), .Q(out_3), .clk(in_1));  // open: carry, clr
  not not_2 (not_2_out, out_3[1]);
  not not_3 (not_3_out, out_3[0]);
  not not_4 (not_4_out, out_3[1]);
  not not_5 (not_5_out, out_3[2]);
  not not_6 (not_6_out, out_3[2]);
  not not_7 (not_7_out, out_3[0]);
  not not_8 (not_8_out, out_3[1]);
  not not_9 (not_9_out, out_3[0]);
  not not_10 (not_10_out, out_3[2]);
  ROM #(.addrWidth(4)) rom_1 (.addr(in_2), .data(rom_1_data), .sel(1'b1));
  and and_1 (and_1_out, out_3[0], not_2_out, out_3[2]);
  and and_2 (and_2_out, not_3_out, not_4_out, not_5_out);
  and and_3 (and_3_out, out_3[0], out_3[1], not_6_out);
  and and_4 (and_4_out, not_7_out, not_8_out, out_3[2]);
  and and_5 (and_5_out, not_9_out, out_3[1], not_10_out);
  not not_11 (not_11_out, and_5_out);
  Counter counter_2 (
    .load(and_5_out), .D(rom_1_data), .count(not_11_out), .Q(counter_2_q), .clk(in_1), .clr(and_2_out));  // open: carry
  or or_1 (or_1_out, and_1_out, and_3_out, and_4_out);
  Multiplexer #(.width(8)) multiplexer_1 (
    .in0(out_3), .in1(counter_2_q), .out(multiplexer_1_out), .sel(or_1_out));  // open: en
  ROM #(.dataWidth(16)) rom_2 (.addr(multiplexer_1_out), .data(out_4), .sel(1'b1));

  // Notes on the sheet:
  //   in_1: pull=up
  //   contents of rom_1 (hex, n*v repeats v):
  //   3 6 9 c 11*0 ff
  //   contents of rom_2 (hex, n*v repeats v):
  //   6 1 18 24 48 0 24 2008 1040 24 2008 1140 4080 8000 8000 240*0 ffff
endmodule

module CPU (
);

  wire ALU_0, ALU_1, ALU_2, ALU_3, and_1_out, CE, clock_1_out, controlled_buffer_1_out, Cp, Ea, Ei, Ep, Eu,
       HLT, La, Lb, LI, Li_t, Lm, Lo, not_1_out, not_2_out, not_3_out, x;
  wire [3:0] counter_1_q, MAR_q, PC_q;
  wire [7:0] a_q, ALU_out_4, b_q, controlled_buffer_2_out, CU_out_3, IR_q, out_q, rom_1_data;

  Clock clock_1 (.out(clock_1_out));
  assign controlled_buffer_1_out = HLT ? clock_1_out : 1'bz;  // Controlled_Buffer controlled_buffer_1
  Counter #(.width(4), .max('hf)) counter_1 (
    .D(4'b0000), .count(and_1_out), .Q(counter_1_q), .clk(controlled_buffer_1_out));  // open: load, carry, clr
  Register #(.width(4)) PC (.D(counter_1_q), .en(Cp), .Q(PC_q), .clk(controlled_buffer_1_out));  // open: clr
  assign controlled_buffer_2_out[3:0] = Ep ? PC_q : 4'bz;  // Controlled_Buffer controlled_buffer_2
  Register IR (.D(controlled_buffer_2_out), .en(LI), .Q(IR_q), .clk(controlled_buffer_1_out));  // open: clr
  Register #(.width(4)) MAR (
    .D(controlled_buffer_2_out[3:0]), .en(Lm), .Q(MAR_q), .clk(controlled_buffer_1_out));  // open: clr
  ROM #(.addrWidth(4)) rom_1 (.addr(MAR_q), .data(rom_1_data), .sel(1'b1));
  assign controlled_buffer_2_out = CE ? rom_1_data : 8'bz;  // Controlled_Buffer controlled_buffer_3
  assign controlled_buffer_2_out[3:0] = Ei ? IR_q[3:0] : 4'bz;  // Controlled_Buffer controlled_buffer_4
  CU CU (
    .in_1(controlled_buffer_1_out), .in_2(IR_q[7:4]), .out_3(CU_out_3),
    .out_4({x, Lo, Lb, Eu, ALU_3, ALU_2, ALU_1, ALU_0, Ea, La, Li_t, Ei, CE, Lm, Ep, Cp}));
  Register b (.D(controlled_buffer_2_out), .en(Lb), .Q(b_q), .clk(controlled_buffer_1_out));  // open: clr
  Register out (.D(controlled_buffer_2_out), .en(Lo), .Q(out_q), .clk(controlled_buffer_1_out));  // open: clr
  assign controlled_buffer_2_out = Ea ? a_q : 8'bz;  // Controlled_Buffer controlled_buffer_5
  Register a (.D(controlled_buffer_2_out), .en(La), .Q(a_q), .clk(controlled_buffer_1_out));  // open: clr
  ALU ALU (.in_1(a_q), .in_2(b_q), .in_3({ALU_3, ALU_2, ALU_1, ALU_0}), .out_4(ALU_out_4));
  assign controlled_buffer_2_out = Eu ? ALU_out_4 : 8'bz;  // Controlled_Buffer controlled_buffer_6
  Hex_Digit_Display hex_digit_display_1 (.value(out_q[3:0]));  // open: dp
  Hex_Digit_Display hex_digit_display_2 (.value(out_q[7:4]));  // open: dp
  not not_1 (not_1_out, CU_out_3[0]);
  not not_2 (not_2_out, CU_out_3[1]);
  not not_3 (not_3_out, CU_out_3[2]);
  and and_1 (and_1_out, not_1_out, not_2_out, not_3_out);
  nand nand_1 (HLT, Cp, Ep, Lm, CE, Ei, Li_t, La, Ea, ALU_0, ALU_1, ALU_2, ALU_3, Eu, Lb, Lo, x);

  // Notes on the sheet:
  //   contents of rom_1 (hex, n*v repeats v):
  //   8 19 1a 2b 30 ff 0 0 3 4 7 5
endmodule
